// Logisim project ALU Control Unit.circ as structural Verilog: 1 circuit, main circuit main
module main (
  input  [1:0] ALUOp,
  input  [2:0] Funct,
  output [2:0] out_3
);

  wire and_1_out, not_1_out, not_2_out;

  and and_1 (and_1_out, ALUOp[1], Funct[1]);
  not not_1 (not_1_out, ALUOp[1]);
  not not_2 (not_2_out, Funct[2]);
  or or_1 (out_3[2], ALUOp[0], and_1_out);
  or or_2 (out_3[1], not_1_out, not_2_out);
  and and_2 (out_3[0], ALUOp[1], Funct[0]);
endmodule
