// Logisim project ALU.circ as structural Verilog: 2 circuits, main circuit main
module main (
  input  A,
  input  B,
  input  cin,
  input  less,
  input  [1:0] ALU_Op,
  input  B_Inv,
  output Result,
  output set,
  output cout
);

  wire and_1_out, multiplexer_1_out, not_1_out, or_1_out;

  not not_1 (not_1_out, B);
  Multiplexer multiplexer_1 (.in0(B), .in1(not_1_out), .out(multiplexer_1_out), .sel(B_Inv));  // open: en
  Adder #(.width(1)) adder_1 (.a(A), .b(multiplexer_1_out), .out(set), .cin(cin), .cout(cout));
  and and_1 (and_1_out, A, B);
  or or_1 (or_1_out, A, B);
  Multiplexer #(.select(2)) multiplexer_2 (
    .in0(and_1_out), .in1(or_1_out), .in2(set), .in3(less), .out(Result), .sel(ALU_Op));  // open: en
endmodule

module _16_bit_alu (
  input  [15:0] B,
  input  [15:0] A,
  input  B_Inv,
  input  Cin,
  input  [1:0] ALU_Op,
  output [15:0] result,
  output zero,
  output Overflow
);

  wire and_1_out, main_1_cout, main_2_cout, main_3_cout, main_4_cout, main_5_cout, main_6_cout, main_7_cout,
       main_8_cout, main_9_cout, main_10_cout, main_11_cout, main_12_cout, main_13_cout, main_14_cout,
       main_15_cout, main_16_cout, main_16_set;
  wire [15:0] divider_1_out, main_1_result, multiplexer_1_out, multiplier_1_out;

  main main_1 (
    .ALU_Op(ALU_Op), .B_Inv(B_Inv), .cout(main_1_cout), .A(A[0]), .B(B[0]), .cin(Cin),
    .Result(main_1_result[0]), .less(main_16_set));  // open: set
  main main_2 (
    .ALU_Op(ALU_Op), .B_Inv(B_Inv), .cout(main_2_cout), .A(A[1]), .B(B[1]), .cin(main_1_cout),
    .Result(main_1_result[1]), .less(1'b0));  // open: set
  main main_3 (
    .ALU_Op(ALU_Op), .B_Inv(B_Inv), .cout(main_3_cout), .A(A[2]), .B(B[2]), .cin(main_2_cout),
    .Result(main_1_result[2]), .less(1'b0));  // open: set
  main main_4 (
    .ALU_Op(ALU_Op), .B_Inv(B_Inv), .cout(main_4_cout), .A(A[3]), .B(B[3]), .cin(main_3_cout),
    .Result(main_1_result[3]), .less(1'b0));  // open: set
  main main_5 (
    .ALU_Op(ALU_Op), .B_Inv(B_Inv), .cout(main_5_cout), .A(A[4]), .B(B[4]), .cin(main_4_cout),
    .Result(main_1_result[4]), .less(1'b0));  // open: set
  main main_6 (
    .ALU_Op(ALU_Op), .B_Inv(B_Inv), .cout(main_6_cout), .A(A[5]), .B(B[5]), .cin(main_5_cout),
    .Result(main_1_result[5]), .less(1'b0));  // open: set
  main main_7 (
    .ALU_Op(ALU_Op), .B_Inv(B_Inv), .cout(main_7_cout), .A(A[6]), .B(B[6]), .cin(main_6_cout),
    .Result(main_1_result[6]), .less(1'b0));  // open: set
  main main_8 (
    .ALU_Op(ALU_Op), .B_Inv(B_Inv), .cout(main_8_cout), .A(A[7]), .B(B[7]), .cin(main_7_cout),
    .Result(main_1_result[7]), .less(1'b0));  // open: set
  main main_9 (
    .ALU_Op(ALU_Op), .B_Inv(B_Inv), .cout(main_9_cout), .A(A[8]), .B(B[8]), .cin(main_8_cout),
    .Result(main_1_result[8]), .less(1'b0));  // open: set
  main main_10 (
    .ALU_Op(ALU_Op), .B_Inv(B_Inv), .cout(main_10_cout), .A(A[9]), .B(B[9]), .cin(main_9_cout),
    .Result(main_1_result[9]), .less(1'b0));  // open: set
  main main_11 (
    .ALU_Op(ALU_Op), .B_Inv(B_Inv), .cout(main_11_cout), .A(A[10]), .B(B[10]), .cin(main_10_cout),
    .Result(main_1_result[10]), .less(1'b0));  // open: set
  main main_12 (
    .ALU_Op(ALU_Op), .B_Inv(B_Inv), .cout(main_12_cout), .A(A[11]), .B(B[11]), .cin(main_11_cout),
    .Result(main_1_result[11]), .less(1'b0));  // open: set
  main main_13 (
    .ALU_Op(ALU_Op), .B_Inv(B_Inv), .cout(main_13_cout), .A(A[12]), .B(B[12]), .cin(main_12_cout),
    .Result(main_1_result[12]), .less(1'b0));  // open: set
  main main_14 (
    .ALU_Op(ALU_Op), .B_Inv(B_Inv), .cout(main_14_cout), .A(A[13]), .B(B[13]), .cin(main_13_cout),
    .Result(main_1_result[13]), .less(1'b0));  // open: set
  main main_15 (
    .ALU_Op(ALU_Op), .B_Inv(B_Inv), .cout(main_15_cout), .A(A[14]), .B(B[14]), .cin(main_14_cout),
    .Result(main_1_result[14]), .less(1'b0));  // open: set
  main main_16 (
    .ALU_Op(ALU_Op), .B_Inv(B_Inv), .cout(main_16_cout), .A(A[15]), .B(B[15]), .cin(main_15_cout),
    .Result(main_1_result[15]), .less(1'b0), .set(main_16_set));
  xor xor_1 (Overflow, main_15_cout, main_16_cout);
  Divider #(.width(16)) divider_1 (.a(A), .b(B), .out(divider_1_out));  // open: upper, rem
  Multiplier #(.width(16)) multiplier_1 (.a(A), .b(B), .out(multiplier_1_out));  // open: cin, cout
  and and_1 (and_1_out, ALU_Op[0], ALU_Op[1]);
  nor nor_1 (zero, main_1_result[0], main_1_result[1], main_1_result[2], main_1_result[3], main_1_result[4], main_1_result[5], main_1_result[6], main_1_result[7], main_1_result[8], main_1_result[9], main_1_result[10], main_1_result[11], main_1_result[12], main_1_result[13], main_1_result[14], main_1_result[15]);
  Multiplexer #(.width(16)) multiplexer_1 (
    .in0(divider_1_out), .in1(multiplier_1_out), .out(multiplexer_1_out), .sel(B_Inv));  // open: en
  Multiplexer #(.width(16)) multiplexer_2 (
    .in0(main_1_result), .in1(multiplexer_1_out), .out(result), .sel(and_1_out));  // open: en
endmodule
